# Fritzing sketch TinyDimmer (saved by Fritzing 0.9.4)
perfboards: 1

parts:
  U1 = attiny85 [package=dip]
  J1 = female pin header, 6 pins [form="♀ (female)"]
  J3 = female pin header, 1 pin [form="♀ (female)"]
  J4 = female pin header, 3 pins [form="♀ (female)"]
  J2 = female pin header, 2 pins [form="♀ (female)"]
  J5 = female pin header, 1 pin [form="♀ (female)"]

nets:
  N1: U1.Pin_1, J1.pin1
  N2: U1.Pin_3, J3.pin1
  N3: U1.Pin_5, J1.pin3
  N4: U1.Pin_6, J1.pin4
  N5: U1.Pin_7, J1.pin5, J5.pin1
  N6: J1.pin2, J4.pin3
  N7: J1.pin6, J2.pin2

notes:
  Yellow - RESET
  Black - GND
  Cyan - MOSI
  Green - MISO
  Orange - SCK
  Red - VCC
